# Fritzing sketch 220v c1 (saved by Fritzing 0.9.3b)
perfboards: 1

parts:
  U1 = NodeMCU V1.0
  Part1 = Solid State High Level Relay Module [package=relay]  # not connected
  Power_plug1 = Power plug  # not connected
  HLK-PM1 = HLK-PM12 [part_number=HLK-PM12]  # not connected
  LED1 = LED - 5mm [color="Red (633nm)" package="5 mm [THT]"]  # not connected

nets:
  N1: U1.D6, U1.D7, U1.GND

custom parts:
  NodeMCU V1.0: ESP8266 based NodeMCU V1.0
  Solid State High Level Relay Module: 5V Omron solid state relay 240V 2A output with resistance fuse.
