# Fritzing sketch 220v c2 (saved by Fritzing 0.9.3b)
perfboards: 1

parts:
  U2 = NodeMCU V1.0
  Part2 = Solid State High Level Relay Module [package=relay]  # not connected
  Power_plug2 = Power plug  # not connected
  HLK-PM2 = HLK-PM12 [part_number=HLK-PM12]  # not connected
  LED2 = LED - 5mm [color="Red (633nm)" package="5 mm [THT]"]  # not connected
  Power_plug3 = Power plug  # not connected

nets:
  N1: U2.D6, U2.D7, U2.GND

custom parts:
  NodeMCU V1.0: ESP8266 based NodeMCU V1.0
  Solid State High Level Relay Module: 5V Omron solid state relay 240V 2A output with resistance fuse.
