# Fritzing sketch 220v (saved by Fritzing 0.9.3b)

parts:
  U1 = NodeMCU V1.0
  Part1 = Solid State High Level Relay Module [package=relay]
  LED1 = smd LED [color="Red (633nm)" package="1206 [SMD]"]
  Power_plug1 = Power plug
  LED2 = LEDs [package=led10mm]
  HLK-PM1 = HLK-PM01

nets:
  N1: U1.D1, U1.D6, U1.D7, U1.TX, U1.GND#13, LED1.cathode, LED1.anode
  N2: U1.Vin, HLK-PM1.+Vo
  N3: U1.GND#16, HLK-PM1.-Vo
  N4: Part1.A1, Power_plug1.GND
  N5: Part1.B1, LED2.C
  N6: Power_plug1.VCC, LED2.A

notes:
  input ไฟ AC 220V

custom parts:
  NodeMCU V1.0: ESP8266 based NodeMCU V1.0
  Solid State High Level Relay Module: 5V Omron solid state relay 240V 2A output with resistance fuse.
  LEDs: LEDs Standard schematic elements and footprints for 5mm, 3mm, 1206, and 0603 sized LEDs. 5mm - Spark Fun Electronics SKU : COM-00529 (and others)
