# Fritzing sketch bulb_plug (saved by Fritzing 0.9.3b)

parts:
  Power_plug1 = Power plug
  U1 = RELAY [package=relay-jzc]
  HLK-PM1 = HLK-PM01
  D1 = LTE-302 [package=lte-302]
  U2 = NodeMCU V1.0
  Part1 = ACS712 Low Current Sensor Board v12
  หลอดไฟ = LEDs [package=led10mm]

nets:
  N1: Power_plug1.GND, HLK-PM1.AC#0, Part1.IP+, หลอดไฟ.C
  N2: Power_plug1.VCC, U1.NC, HLK-PM1.AC#1
  N3: U1.COIL2, HLK-PM1.-Vo, U2.GND#16, Part1.GND
  N4: U1.NO, Part1.IP-, หลอดไฟ.A
  N5: U1.MAIN, D1.A, D1.C, U2.D1, U2.D7, U2.D8, U2.GND#13
  VIN: U1.COIL1, HLK-PM1.+Vo, U2.Vin, Part1.5V
  N6: U2.A0, Part1.VO

custom parts:
  NodeMCU V1.0: ESP8266 based NodeMCU V1.0
  LEDs: LEDs Standard schematic elements and footprints for 5mm, 3mm, 1206, and 0603 sized LEDs. 5mm - Spark Fun Electronics SKU : COM-00529 (and others)
