# Fritzing sketch pir sensor (saved by Fritzing 0.9.3b)

parts:
  Raspberry_Pi_1 = Raspberry Pi 3 [part_number=RPI-3-V1.2]
  PIR1 = PIR sensor
  CAMERA1 = TTL Serial JPEG Camera  # not connected

nets:
  N1: Raspberry_Pi_1.GPIO17, PIR1.GND
  N2: Raspberry_Pi_1.GND, PIR1.SIG
  5V: Raspberry_Pi_1.5V, PIR1.VDD

notes:
  Adapter 5V 1A
  Pi camera
  PIR Sensor

custom parts:
  TTL Serial JPEG Camera: TTL Serial JPEG Camera with NTSC Out
